// Logisim project IT012_Lab01_25522081.circ as structural Verilog
module Warmup (
  input  A,
  input  B,
  output F
);

  wire not_1_out;

  not not_1 (not_1_out, B);
  and and_1 (F, A, not_1_out);
endmodule

module TN1 (
  input  A,
  input  B,
  input  C,
  output NOT,
  output AND,
  output OR,
  output NAND,
  output NOR,
  output XOR,
  output XNOR,
  output XOR3,
  output NAND3,
  output CHAIN
);

  wire nand_1_out;

  nand nand_1 (nand_1_out, A, B);
  not not_1 (NOT, A);
  and and_1 (AND, A, B);
  or or_1 (OR, A, B);
  nand nand_2 (NAND, A, B);
  nor nor_1 (NOR, A, B);
  xor xor_1 (XOR, A, B);
  xor xor_2 (XOR3, A, B, C);
  nand nand_3 (NAND3, A, B, C);
  nand nand_4 (CHAIN, nand_1_out, C);
  xnor xnor_1 (XNOR, A, B);
endmodule

module TN2 (
  input  x,
  input  y,
  input  z,
  output EQ1,
  output EQ2,
  output EQ3,
  output EQ4,
  output EQ5
);

  wire and_1_out, and_2_out, and_3_out, and_4_out, and_5_out, and_6_out, not_1_out, not_2_out, not_3_out,
       not_4_out, not_5_out, not_6_out, not_7_out, or_1_out, or_2_out, or_3_out, or_4_out, or_5_out, or_6_out;

  not not_1 (not_1_out, x);
  not not_2 (not_2_out, x);
  not not_3 (not_3_out, y);
  not not_4 (not_4_out, x);
  not not_5 (not_5_out, y);
  or or_1 (or_1_out, x, y);
  or or_2 (or_2_out, x, z);
  and and_1 (and_1_out, y, z);
  and and_2 (and_2_out, not_1_out, y);
  or or_3 (or_3_out, x, y);
  and and_3 (and_3_out, not_2_out, not_3_out);
  and and_4 (and_4_out, x, y);
  and and_5 (and_5_out, not_4_out, not_5_out);
  and and_6 (and_6_out, or_1_out, or_2_out);
  or or_4 (or_4_out, x, and_1_out);
  or or_5 (or_5_out, x, and_2_out);
  or or_6 (or_6_out, x, y);
  not not_6 (not_6_out, or_3_out);
  not not_7 (not_7_out, and_4_out);
  xnor xnor_1 (EQ1, not_6_out, and_3_out);
  xnor xnor_2 (EQ2, not_7_out, and_5_out);
  xnor xnor_3 (EQ3, and_6_out, or_4_out);
  xnor xnor_4 (EQ4, x, or_5_out);
  xnor xnor_5 (EQ5, or_5_out, or_6_out);
endmodule

module TN3 (
  input  A,
  input  B,
  input  C,
  input  D,
  output F
);

  wire and_1_out, and_2_out, and_3_out, and_4_out, and_5_out, and_6_out, not_1_out, not_2_out, not_3_out,
       not_4_out;

  not not_1 (not_1_out, A);
  not not_2 (not_2_out, C);
  not not_3 (not_3_out, B);
  not not_4 (not_4_out, D);
  and and_1 (and_1_out, not_1_out, not_3_out, C, not_4_out);
  and and_2 (and_2_out, not_1_out, not_3_out, C, D);
  and and_3 (and_3_out, not_1_out, B, not_2_out, D);
  and and_4 (and_4_out, not_1_out, B, C, D);
  and and_5 (and_5_out, A, not_3_out, C, D);
  and and_6 (and_6_out, A, B, not_2_out, D);
  or or_1 (F, and_1_out, and_2_out, and_3_out, and_4_out, and_5_out, and_6_out);
endmodule

module TN4 (
  input  A,
  input  B,
  input  C,
  input  D,
  output F_can,
  output EQ1,
  output F_sop,
  output EQ2,
  output F_pos
);

  wire A_prime_B_prime_C_out, A_prime_B_prime_C_prime_out, A_prime_CD_out, A_prime_D_out, and_1_out,
       and_2_out, and_3_out, and_4_out, and_5_out, and_6_out, B_C_out, B_prime_CD_out, B_prime_D_out,
       BC_prime_D_out, not_1_out, not_2_out, not_3_out, not_4_out;

  not not_1 (not_1_out, A);
  not not_2 (not_2_out, C);
  not not_3 (not_3_out, B);
  not not_4 (not_4_out, D);
  and and_1 (and_1_out, not_1_out, not_3_out, C, not_4_out);
  and and_2 (and_2_out, not_1_out, not_3_out, C, D);
  and and_3 (and_3_out, not_1_out, B, not_2_out, D);
  and and_4 (and_4_out, not_1_out, B, C, D);
  and and_5 (and_5_out, A, not_3_out, C, D);
  and and_6 (and_6_out, A, B, not_2_out, D);
  and A_prime_B_prime_C (A_prime_B_prime_C_out, not_1_out, not_3_out, C);
  and A_prime_CD (A_prime_CD_out, not_1_out, C, D);
  and B_prime_CD (B_prime_CD_out, not_3_out, C, D);
  and BC_prime_D (BC_prime_D_out, B, not_2_out, D);
  or B_prime_D (B_prime_D_out, not_3_out, D);
  or A_prime_D (A_prime_D_out, not_1_out, D);
  or A_prime_B_prime_C_prime (A_prime_B_prime_C_prime_out, not_1_out, not_3_out, not_2_out);
  or B_C (B_C_out, B, C);
  or or_1 (F_can, and_1_out, and_2_out, and_3_out, and_4_out, and_5_out, and_6_out);
  or or_2 (F_sop, A_prime_B_prime_C_out, A_prime_CD_out, B_prime_CD_out, BC_prime_D_out);
  and and_7 (F_pos, A_prime_D_out, A_prime_B_prime_C_prime_out, B_prime_D_out, B_C_out);
  xnor xnor_1 (EQ1, F_can, F_sop);
  xnor xnor_2 (EQ2, F_can, F_pos);
endmodule

module TN5 (
  input  A,
  input  B,
  input  C,
  output F
);

  wire xor_1_out;

  xor xor_1 (xor_1_out, A, B);
  xor xor_2 (F, xor_1_out, C);
endmodule
